# Fritzing sketch KIK01_LED_Board 2 (saved by Fritzing 0.9.3b)
breadboards: 1

parts:
  J1 = STM32 Nucleo boards
  R1 = Resistor [tolerance=±5% resistance=100 package=THT]
  R2 = Resistor [tolerance=±5% resistance=220 package=THT]
  R3 = Resistor [tolerance=±5% resistance=470 package=THT]
  R4 = Resistor [tolerance=±5% resistance=1k package=THT]  # not connected
  LED1 = LED - 3mm [color="Green (555nm)" package="3 mm [THT]"]
  LED2 = LED - 3mm [color="Red (633nm)" package="3 mm [THT]"]
  LED3 = LED - 3mm [color="Blue (525nm)" package="3 mm [THT]"]
  LED4 = LED - 3mm [color="Yellow (595nm)" package="3 mm [THT]"]
  S2 = Toggle Switch [package=THT]
  R7 = Resistor [tolerance=±5% resistance=100 package=THT]
  S3 = Toggle Switch [package=THT]

nets:
  N1: J1.PA12, R2.Pin_0
  N2: J1.PA11, R3.Pin_0
  N3: J1.PB12, R1.Pin_0
  N4: J1.GND, LED1.cathode, LED2.cathode, LED3.cathode, LED4.cathode
  N5: J1.PB2, S2.COM
  N6: J1.PB1, S3.COM
  N7: R1.Pin_1, LED3.anode
  N8: R2.Pin_1, LED2.anode
  N9: R3.Pin_1, LED4.anode
  N10: R7.Pin_0, S3.L2

notes:
  LEDs
  Beat
  SyncIn
  SyncOut
  Power
  AutoRunSw
  GND
